# Fritzing sketch Wiring_trigger (saved by Fritzing 0.9.10b)

parts:
  M2 = fc-51 [package=THT]
  Bauteil2 = Arduino Uno (Rev3) - ICSP

nets:
  N1: M2.pin1, Bauteil2.D3_PWM
  N2: M2.pin2, Bauteil2.GND
  N3: M2.pin3, Bauteil2.3V3

notes:
  HW201
