# Fritzing sketch wiring_uart_uno_to_uno (saved by Fritzing 0.9.10b)
breadboards: 2

parts:
  Bauteil2 = Arduino Uno (Rev3) - ICSP
  Bauteil3 = Arduino Uno (Rev3) - ICSP
  S2 = Momentary Switch [package=ksa_sealed_tac_switch]
  R1 = Resistor [tolerance=±5% resistance=220 package="0603 [SMD]"]
  LED1 = LED - 5mm [color="Red (633nm)" current=0.030 package="5 mm [THT]"]

nets:
  N1: Bauteil2.D4, S2.1
  N2: Bauteil2.D5_PWM, Bauteil3.D3_PWM
  N3: Bauteil2.D6_PWM, Bauteil3.D2
  N4: Bauteil2.5V, S2.4
  GND: Bauteil2.GND, Bauteil3.GND, R1.Pin_1, LED1.cathode
  N5: Bauteil3.D6_PWM, LED1.anode
  N6: S2.2, R1.Pin_0

notes:
  10k
  ~220 Ohm
