# Fritzing sketch wiring_uart_uno_to_esp32 (saved by Fritzing 0.9.10b)
breadboards: 2

parts:
  Bauteil2 = Arduino Uno (Rev3) - ICSP
  S2 = Momentary Switch [package=ksa_sealed_tac_switch]
  R1 = Resistor [tolerance=±5% resistance=220 package="0603 [SMD]"]
  LED1 = LED - 5mm [color="Red (633nm)" current=0.030 package="5 mm [THT]"]
  MH-ET_Live_Minikit_for_ESP1 = MH-ET Live Minikit for ESP32
  Bauteil5 = I2C level shifter bidirectional  # not connected
  R2 = Resistor [tolerance=±5% resistance=220 package="0603 [SMD]"]

nets:
  N1: Bauteil2.GND, R1.Pin_1
  N2: Bauteil2.D4, S2.1
  N3: Bauteil2.5V, S2.4
  N4: S2.2, R1.Pin_0
  N5: LED1.cathode, MH-ET_Live_Minikit_for_ESP1.GND
  N6: LED1.anode, R2.Pin_0
  N7: MH-ET_Live_Minikit_for_ESP1.IO4, R2.Pin_1

notes:
  10k
  ~220 Ohm

custom parts:
  MH-ET Live Minikit for ESP32: MH-ET Live Minikit for ESP32 ( http://mh.nodebb.com/topic/8/mh-et-live-minikit-for-esp32/2/) PCB footprint is invalid.
