# Fritzing sketch wiring_dht11 (saved by Fritzing 0.9.10b)
breadboards: 1

parts:
  U1 = ESP32-38PinWide [part_number=ESP32-38PinWide]
  A6 = DHT22 module
  DHT11_1 = DHT11 module

nets:
  N1: U1.GPIO26, DHT11_1.DATA
  VIN: U1.VIN, A6.+, DHT11_1.VCC
  N2: U1.GPIO5, A6.Out
  GND: U1.GND, A6.-, DHT11_1.GND

custom parts:
  ESP32-38PinWide: Generic 38-Pin ESP32 with wide format (only access to one side of pins on a breadboard) based on Stephen Lilley's HiLetgo ESP-WROOM-32 ESP32 ESP-32S Development Board.
  DHT22 module: DHT22 module. Pins VCC Data GND.
  DHT11 module: https://cdn-learn.adafruit.com/downloads/pdf/dht.pdf DHT11 black pcb module reference by:https://github.com/adafruit/Fritzing-Library/blob/master/parts/DHT11%20Humitidy%20and%20Temperature%20Sensor.fzpz
