# Fritzing sketch wiring_dht22_spi (saved by Fritzing 0.9.10b)

parts:
  A6 = DHT22 module
  Bauteil1 = Arduino Uno (Rev3) - ICSP
  Bauteil2 = Arduino Uno (Rev3) - ICSP

nets:
  N1: A6.+, Bauteil1.3V3
  N2: A6.Out, Bauteil1.D5_PWM
  GND: A6.-, Bauteil1.GND, Bauteil2.GND
  N3: Bauteil1.D10_PWM/SS, Bauteil2.D10_PWM/SS
  N4: Bauteil1.D11_PWM/MOSI, Bauteil2.D11_PWM/MOSI
  N5: Bauteil1.D12/MISO, Bauteil2.D12/MISO
  N6: Bauteil1.D13/SCK, Bauteil2.D13/SCK

custom parts:
  DHT22 module: DHT22 module. Pins VCC Data GND.
