# Fritzing sketch i2cWiring (saved by Fritzing 0.9.10b)
breadboards: 1

parts:
  MH-ET_Live_Minikit_for_ESP1 = MH-ET Live Minikit for ESP32
  A5 = DHT22 module
  o1 = Module display OLED I2C 128x64 SSD1306 [package=THT]
  Bauteil1 = BH1750

nets:
  3.3V: MH-ET_Live_Minikit_for_ESP1.3.3V, A5.+, o1.VCC
  N1: MH-ET_Live_Minikit_for_ESP1.IO22, A5.SCL, o1.SCL, Bauteil1.SCL
  N2: MH-ET_Live_Minikit_for_ESP1.IO21, A5.SDA, o1.SDA, Bauteil1.SDA
  GND: MH-ET_Live_Minikit_for_ESP1.GND, MH-ET_Live_Minikit_for_ESP1.SD0, A5.-, o1.GND, Bauteil1.GND

custom parts:
  MH-ET Live Minikit for ESP32: MH-ET Live Minikit for ESP32 ( http://mh.nodebb.com/topic/8/mh-et-live-minikit-for-esp32/2/) PCB footprint is invalid.
  DHT22 module: DHT22 module. Pins VCC Data GND.
  Module display OLED I2C 128x64 SSD1306: Ecran OLED I2C SSD163 de 128x64 avec connexion I2C
  BH1750: Light Sensor
